# Fritzing sketch mont_ldr (saved by Fritzing 0.9.3b)
breadboards: 1

parts:
  R1 = Photocell (LDR) [package=THT]
  R2 = Photocell (LDR) [package=THT]
  Componente1 = node32s
  R3 = Resistor [tolerance=±5% resistance=10k package=THT]
  R4 = Resistor [tolerance=±5% resistance=10k package=THT]

nets:
  N1: R1.pin_0, Componente1.IO25, R3.Pin_1
  N2: R1.pin_1, R2.pin_1, Componente1.GND
  N3: R2.pin_0, Componente1.IO26, R4.Pin_1
  N4: Componente1.3.3V, R3.Pin_0, R4.Pin_0
