# Fritzing sketch mont_lm35 (saved by Fritzing 0.9.3b)
breadboards: 1

parts:
  Componente1 = node32s
  T1 = LM35 Temperature Sensor [package="TO92 [THT]"]

nets:
  N1: Componente1.3.3V, T1.+Vs
  GND: Componente1.GND, T1.GND
  N2: Componente1.IO0, T1.Vout
