# Fritzing sketch mont_servo (saved by Fritzing 0.9.3b)
breadboards: 1

parts:
  Componente1 = node32s
  J1 = Basic Servo

nets:
  N1: Componente1.IO32, J1.pulse
  5V: Componente1.5V, J1.vcc
  GND: Componente1.GND, J1.gnd
