# Fritzing sketch mont_somsensor (saved by Fritzing 0.9.3b)
breadboards: 1

parts:
  Componente1 = node32s
  hc-sr1 = hc-sr04

nets:
  5V: Componente1.5V, hc-sr1.VCC
  GND: Componente1.GND, hc-sr1.GND
  N1: Componente1.IO4, hc-sr1.Trig
  N2: Componente1.IO2, hc-sr1.Echo
